# Fritzing sketch logic (saved by Fritzing 0.9.2b)
breadboards: 2

parts:
  Raspberry_Pi1 = Raspberry Pi 2
  パーツ1 = Arduino Uno (Rev3)
  D1 = LED_BARGRAPH_10 [package=led_bargaph_10]
  7_Segment_4_Digit_Display2 = 7-SEGMENT-4DIGIT common cathode [part_number=HS420561K-32 package=7-segment-4digit-cathode]
  A = Pushbutton [package="[THT]"]
  B = Pushbutton [package="[THT]"]
  C = Pushbutton [package="[THT]"]
  D = Pushbutton [package="[THT]"]
  E = Pushbutton [package="[THT]"]
  R1 = PHOTOCELL [package=photocell]
  ACT = smd LED [color="Green (570nm)" package="1206 [SMD]"]
  R2 = Resistor [tolerance=±5% resistance=10k package=THT]
  R3 = Resistor [tolerance=±5% resistance=100 package=THT]
  FAIL = smd LED [color="Red (633nm)" package="1206 [SMD]"]
  R4 = Resistor [tolerance=±5% resistance=680 package=THT]
  R5 = Resistor [tolerance=±5% resistance=680 package=THT]
  R6 = Resistor [tolerance=±5% resistance=68k package=THT]
  R7 = Resistor [tolerance=±5% resistance=680 package=THT]
  R8 = Resistor [tolerance=±5% resistance=10k package=THT]
  R9 = Resistor [tolerance=±5% resistance=10k package=THT]
  R10 = Resistor [tolerance=±5% resistance=100 package=THT]
  R11 = Resistor [tolerance=±5% resistance=100 package=THT]
  R12 = Resistor [tolerance=±5% resistance=100 package=THT]
  R13 = Resistor [tolerance=±5% resistance=100 package=THT]
  ENT = Pushbutton [package="[THT]"]

nets:
  N1: Raspberry_Pi1.GPIO4, D1.D_A
  N2: Raspberry_Pi1.GPIO17, D1.E_A
  N3: Raspberry_Pi1.GPIO27, D1.F_A
  N4: Raspberry_Pi1.GPIO10, パーツ1.D11_PWM/MOSI
  N5: Raspberry_Pi1.GPIO9, R8.Pin_0, R9.Pin_1
  N6: Raspberry_Pi1.GPIO11, R6.Pin_1, R7.Pin_0
  N7: Raspberry_Pi1.GPIO5, A.Pin_3, A.Pin_4
  N8: Raspberry_Pi1.GPIO6, B.Pin_3, B.Pin_4
  N9: Raspberry_Pi1.GPIO13, C.Pin_3, C.Pin_4
  N10: Raspberry_Pi1.GPIO19, D.Pin_3, D.Pin_4
  N11: Raspberry_Pi1.GPIO26, E.Pin_3, E.Pin_4
  N12: Raspberry_Pi1.GPIO12, ENT.Pin_3, ENT.Pin_4
  N13: Raspberry_Pi1.GPIO8, パーツ1.D10_PWM/SS
  N14: Raspberry_Pi1.GPIO24, R5.Pin_1
  N15: Raspberry_Pi1.GPIO23, R4.Pin_1
  N16: Raspberry_Pi1.GPIO18, D1.G_A
  GND: Raspberry_Pi1.GND, パーツ1.GND, A.Pin_1, A.Pin_2, B.Pin_1, B.Pin_2, C.Pin_1, C.Pin_2, D.Pin_1, D.Pin_2, E.Pin_1, E.Pin_2, ACT.cathode, R2.Pin_0, R3.Pin_0, FAIL.cathode, R6.Pin_0, R9.Pin_0, ENT.Pin_1, ENT.Pin_2
  N17: パーツ1.A0, R10.Pin_1
  N18: パーツ1.A1, R12.Pin_1
  N19: パーツ1.A5/SCL, R1.P$1, R2.Pin_1
  N20: パーツ1.D8, R13.Pin_0
  N21: パーツ1.D9_PWM, R11.Pin_1
  N22: パーツ1.D12/MISO, R8.Pin_1
  N23: パーツ1.D13/SCK, R7.Pin_1
  N24: パーツ1.D0/RX, 7_Segment_4_Digit_Display2.pin_11
  N25: パーツ1.D1/TX, 7_Segment_4_Digit_Display2.pin_7
  N26: パーツ1.D2, 7_Segment_4_Digit_Display2.pin_4
  N27: パーツ1.D3_PWM, 7_Segment_4_Digit_Display2.pin_2
  N28: パーツ1.D4, 7_Segment_4_Digit_Display2.pin_1
  N29: パーツ1.D5_PWM, 7_Segment_4_Digit_Display2.pin_10
  N30: パーツ1.D6_PWM, 7_Segment_4_Digit_Display2.pin_5
  N31: パーツ1.D7, 7_Segment_4_Digit_Display2.pin_3
  N32: パーツ1.5V, R1.P$2
  N33: D1.G_C, D1.F_C, D1.E_C, D1.D_C, R3.Pin_1
  N34: 7_Segment_4_Digit_Display2.pin_6, R12.Pin_0
  N35: 7_Segment_4_Digit_Display2.pin_8, R10.Pin_0
  N36: 7_Segment_4_Digit_Display2.pin_9, R11.Pin_0
  N37: 7_Segment_4_Digit_Display2.pin_12, R13.Pin_1
  N38: ACT.anode, R4.Pin_0
  N39: FAIL.anode, R5.Pin_0

custom parts:
  7-SEGMENT-4DIGIT common cathode: A 7 Segment 4 Digit common cathode display, with decimal points
